# Fritzing sketch CIRCUIT (saved by Fritzing 0.9.3b)

parts:
  H2 = polarizedheader 4pin 0.156in [package=THT]
  LED2 = RGB LED (com. cathode, rbg) [package="5 mm [THT]"]  # not connected
  U1 = NodeMCU V1.0

nets:
  N1: H2.pin2, U1.GND
  N2: H2.pin3, U1.3V3
  N3: H2.pin4, U1.D5

notes:
  NODEMCU - MQ-135
  GND - GND
  VCC - VIN
  AO - A0
  NODEMCU - MICROPHONE
  GND - GND
  VCC - VCC
  DO - D5

custom parts:
  polarizedheader 4pin 0.156in: .156” CENTERS LOCKING POLARIZED HEADERS
  RGB LED (com. cathode, rbg): A 5mm tri-color LED with red, green and blue inside. Pin order: red - com. cathode - blue - green
  NodeMCU V1.0: ESP8266 based NodeMCU
